// Logisim project RAMTASTIC!!!!.circ as structural Verilog
module main (
  input  [2:0] in_1,
  input  in_2,
  input  in_3,
  input  in_4,
  input  R_W,
  input  in_6,
  input  in_7,
  input  in_8,
  input  in_9,
  output [3:0] out_10,
  output [3:0] curent_data
);

  wire clock_1_out, r_w_register_1_output;
  wire [1:0] n2_bit_register_1_output;
  wire [2:0] or_1_out;

  assign or_1_out = in_1 | {3{in_2}};  // OR_Gate or_1, 3 bits wide
  Clock clock_1 (.out(clock_1_out));
  RAM ram_1 (
    .out_9(out_10), .in_4(n2_bit_register_1_output), .in_1(r_w_register_1_output), .in_2(curent_data),
    .Clock(clock_1_out));  // open: out_5, out_6, out_7, out_8
  _2_Bit_Register u_2_bit_register_1 (
    .Clock(clock_1_out), .Enable(or_1_out[2]), .Output(n2_bit_register_1_output), .Input({in_3, in_4}));
  R_W_Register r_w_register_1 (.Clock(clock_1_out), .Enable(or_1_out[1]), .Output(r_w_register_1_output), .Input(R_W));
  Data_Register data_register_1 (
    .CPU_Line(or_1_out[0]), .Output(curent_data), .Input({in_6, in_7, in_8, in_9}), .in_2(out_10),
    .R_W_Line(r_w_register_1_output), .Clock(clock_1_out));

  // Notes on the sheet:
  //   CPU LINES
  //   You may in some cases  not want to update the data register, for this it's best to use individual toggle. For example to copy and paste read from an address, then change to write and a new address.
  //   OPERATION INSTRUCTIONS PLEASE READ
  //   FIRST THINGS FIRST GOTO Simulate -> Ticks Enabled
  //   Adress
  //   RAM
  //   Address Register
  //   When using the individual lines, Please follow this order of operations: 010 -> 110 -> 111 (leave out this last step for copy pasting)
  //   R/W Register
  //   Each register is updated when you enable the cpu lines. You can enable all 3 at once with the 1 bit input pin. Or individually in the order of Add.Reg - R/W Reg - Data Reg
  //   Data from BUS
  //   If you get an error PLEASE read the note in RAM sub circuit and the instructions below. It may be an error with logisim that i encountered and is fixed by restarting the program
  //   Data Register
  //   current output from ram
  //   If RAM and BUS are inputing data, RAM gets priority, there is a fail safe in the Data Reg
endmodule

module Bit (
  input  Data,
  input  Enable,
  output out_3
);

  wire and_1_out, and_2_out, not_1_out;

  D_Flip_Flop d_ff_1 (.Q(out_3), .preset(and_1_out), .reset(and_2_out));  // open: clk, D, Qn, en
  and and_1 (and_1_out, Data, Enable);
  not not_1 (not_1_out, Data);
  and and_2 (and_2_out, not_1_out, Enable);
endmodule

module Nibble (
  input  Clock,
  input  Enable,
  input  [3:0] Input,
  output [3:0] Output
);

  D_Flip_Flop d_ff_1 (.clk(Clock), .D(Input[3]), .Q(Output[3]), .en(Enable));  // open: Qn, preset, reset
  D_Flip_Flop d_ff_2 (.clk(Clock), .D(Input[2]), .Q(Output[2]), .en(Enable));  // open: Qn, preset, reset
  D_Flip_Flop d_ff_3 (.clk(Clock), .D(Input[1]), .Q(Output[1]), .en(Enable));  // open: Qn, preset, reset
  D_Flip_Flop d_ff_4 (.clk(Clock), .D(Input[0]), .Q(Output[0]), .en(Enable));  // open: Qn, preset, reset
endmodule

module Addresser (
  input  [1:0] Address,
  output out_2,
  output out_3,
  output out_4,
  output out_5
);

  wire not_1_out, not_2_out, not_3_out, not_4_out;

  not not_1 (not_1_out, Address[0]);
  not not_2 (not_2_out, Address[1]);
  not not_3 (not_3_out, Address[1]);
  not not_4 (not_4_out, Address[0]);
  and and_1 (out_2, not_1_out, not_2_out);
  and and_2 (out_3, Address[0], not_3_out);
  and and_3 (out_4, not_4_out, Address[1]);
  and and_4 (out_5, Address[0], Address[1]);
endmodule

module Read_Switch (
  input  [3:0] _00_input,
  input  [3:0] _01_input,
  input  [3:0] _10_input,
  input  [3:0] _11_input,
  input  Read_Write,
  input  [1:0] Address,
  output [3:0] out_7
);

  wire addresser_1_out_2, addresser_1_out_3, addresser_1_out_4, addresser_1_out_5, and_1_out, and_2_out,
       and_3_out, and_4_out, not_1_out;
  wire [3:0] let_1_out_3, let_2_out_3, let_3_out_3, let_4_out_3;

  Addresser addresser_1 (
    .Address(Address), .out_2(addresser_1_out_2), .out_3(addresser_1_out_3), .out_4(addresser_1_out_4),
    .out_5(addresser_1_out_5));
  Let_Gate let_1 (.Input(_00_input), .Enable(and_2_out), .out_3(let_1_out_3));
  Let_Gate let_2 (.Input(_01_input), .Enable(and_1_out), .out_3(let_2_out_3));
  and and_1 (and_1_out, addresser_1_out_3, not_1_out);
  and and_2 (and_2_out, addresser_1_out_2, not_1_out);
  Let_Gate let_3 (.Input(_10_input), .Enable(and_3_out), .out_3(let_3_out_3));
  and and_3 (and_3_out, addresser_1_out_4, not_1_out);
  Let_Gate let_4 (.Input(_11_input), .Enable(and_4_out), .out_3(let_4_out_3));
  and and_4 (and_4_out, addresser_1_out_5, not_1_out);
  not not_1 (not_1_out, Read_Write);
  assign out_7 = let_1_out_3 | let_2_out_3 | let_3_out_3 | let_4_out_3;  // OR_Gate or_1, 4 bits wide

  // Notes on the sheet:
  //   Merges multiple inputs, checks if read mode is on,  and outputs only the addressed value
endmodule

module Let_Gate (
  input  [3:0] Input,
  input  Enable,
  output [3:0] out_3
);

  and and_1 (out_3[0], Input[0], Enable);
  and and_2 (out_3[1], Input[1], Enable);
  and and_3 (out_3[2], Input[2], Enable);
  and and_4 (out_3[3], Input[3], Enable);

  // Notes on the sheet:
  //   Let's Data Pass through
endmodule

module RAM (
  input  in_1,
  input  [3:0] in_2,
  input  Clock,
  input  [1:0] in_4,
  output [3:0] out_5,
  output [3:0] out_6,
  output [3:0] out_7,
  output [3:0] out_8,
  output [3:0] out_9
);

  wire addresser_1_out_2, addresser_1_out_3, addresser_1_out_4, addresser_1_out_5, and_1_out, and_2_out,
       and_3_out, and_4_out, not_1_out;

  Addresser addresser_1 (
    .Address(in_4), .out_2(addresser_1_out_2), .out_3(addresser_1_out_3), .out_4(addresser_1_out_4),
    .out_5(addresser_1_out_5));
  not not_1 (not_1_out, Clock);
  and and_1 (and_1_out, addresser_1_out_2, in_1);
  and and_2 (and_2_out, addresser_1_out_3, in_1);
  and and_3 (and_3_out, addresser_1_out_4, in_1);
  and and_4 (and_4_out, addresser_1_out_5, in_1);
  Nibble nibble_1 (.Input(in_2), .Output(out_5), .Enable(and_1_out), .Clock(not_1_out));
  Nibble nibble_2 (.Input(in_2), .Output(out_6), .Enable(and_2_out), .Clock(not_1_out));
  Nibble nibble_3 (.Input(in_2), .Output(out_7), .Enable(and_3_out), .Clock(not_1_out));
  Nibble nibble_4 (.Input(in_2), .Output(out_8), .Enable(and_4_out), .Clock(not_1_out));
  Read_Switch read_switch_1 (
    ._00_input(out_5), ._01_input(out_6), ._10_input(out_7), ._11_input(out_8), .Address(in_4),
    .Read_Write(in_1), .out_7(out_9));

  // Notes on the sheet:
  //   To Marker PLEASE READ: When testing this system the top wire out of addresser into 00 nibble had an error
  //   despite it being the EXACT same circuit as 01,10 and 11. This error was a false and restarting LOGISIM fixed the error
  //   If you come across an error in my RAM, please save, restart the program and try again. If the error still persists then it is my fault.
endmodule

module _2_Bit_Register (
  input  Clock,
  input  Enable,
  input  [1:0] Input,
  output [1:0] Output
);

  D_Flip_Flop d_ff_1 (.clk(Clock), .D(Input[1]), .Q(Output[1]), .en(Enable));  // open: Qn, preset, reset
  D_Flip_Flop d_ff_2 (.clk(Clock), .D(Input[0]), .Q(Output[0]), .en(Enable));  // open: Qn, preset, reset
endmodule

module R_W_Register (
  input  Clock,
  input  Enable,
  input  Input,
  output Output
);

  D_Flip_Flop d_ff_1 (.clk(Clock), .D(Input), .Q(Output), .en(Enable));  // open: Qn, preset, reset
endmodule

module _2_Switch (
  input  [3:0] Input_1,
  input  [3:0] Input_2,
  output [3:0] Output,
  output Error
);

  wire or_2_out, or_3_out;

  assign Output = Input_1 | Input_2;  // OR_Gate or_1, 4 bits wide
  or or_2 (or_2_out, Input_1[0], Input_1[1], Input_1[2], Input_1[3]);
  or or_3 (or_3_out, Input_2[0], Input_2[1], Input_2[2], Input_2[3]);
  and and_1 (Error, or_2_out, or_3_out);
endmodule

module Data_Register (
  input  Clock,
  input  [3:0] in_2,
  input  CPU_Line,
  input  R_W_Line,
  input  [3:0] Input,
  output [3:0] Output
);

  wire and_1_out, and_2_out, and_3_out, and_4_out, not_1_out, or_1_out, or_2_out, or_3_out, or_4_out,
       or_5_out;

  not not_1 (not_1_out, R_W_Line);
  or or_1 (or_1_out, CPU_Line, not_1_out);
  or or_2 (or_2_out, and_1_out, in_2[3]);
  and and_1 (and_1_out, Input[3], R_W_Line);
  D_Flip_Flop d_ff_1 (.clk(Clock), .D(or_2_out), .Q(Output[3]), .en(or_1_out));  // open: Qn, preset, reset
  or or_3 (or_3_out, and_2_out, in_2[2]);
  and and_2 (and_2_out, Input[2], R_W_Line);
  D_Flip_Flop d_ff_2 (.clk(Clock), .D(or_3_out), .Q(Output[2]), .en(or_1_out));  // open: Qn, preset, reset
  or or_4 (or_4_out, and_3_out, in_2[1]);
  and and_3 (and_3_out, Input[1], R_W_Line);
  D_Flip_Flop d_ff_3 (.clk(Clock), .D(or_4_out), .Q(Output[1]), .en(or_1_out));  // open: Qn, preset, reset
  D_Flip_Flop d_ff_4 (.clk(Clock), .D(or_5_out), .Q(Output[0]), .en(or_1_out));  // open: Qn, preset, reset
  or or_5 (or_5_out, and_4_out, in_2[0]);
  and and_4 (and_4_out, Input[0], R_W_Line);

  // Notes on the sheet:
  //   PRIORITY CUT OFF! Reading from RAM has priority and cuts off Input
endmodule
